// Digital circuit 4 Bit Register.dig as structural Verilog
module _4_Bit_Register (
  input  [3:0] I_3_0,
  input  CLK,
  output [3:0] O_3_0
);

  _1_Bit_Reg _1_bit_reg_1 (.Din(I_3_0[3]), .SEL(1'b1), .CLK(CLK), .Dout(O_3_0[3]));
  _1_Bit_Reg _1_bit_reg_2 (.Din(I_3_0[2]), .SEL(1'b1), .CLK(CLK), .Dout(O_3_0[2]));
  _1_Bit_Reg _1_bit_reg_3 (.Din(I_3_0[1]), .SEL(1'b1), .CLK(CLK), .Dout(O_3_0[1]));
  _1_Bit_Reg _1_bit_reg_4 (.Din(I_3_0[0]), .SEL(1'b1), .CLK(CLK), .Dout(O_3_0[0]));

  // Other names for the same wires on the sheet: B0 = O_3_0[0]; B1 = O_3_0[1]; B2 = O_3_0[2]; B3 = O_3_0[3];
  //   A0 = I_3_0[0]; A1 = I_3_0[1]; A2 = I_3_0[2]; A3 = I_3_0[3]
endmodule
