// Digital circuit 4Bit PC Adder.dig as structural Verilog
module _4Bit_PC_Adder (
  input  [3:0] I_3_0,
  output [3:0] O_3_0
);

  wire and_1_out, and_2_out, and_3_out, and_4_out, and_5_out, and_6_out, and_7_out, JG8, not_1_out,
       not_2_out, not_3_out, not_4_out, not_5_out, not_6_out, not_7_out, not_8_out, not_9_out, not_10_out,
       not_11_out, not_12_out;
  wire [3:0] multiplexer_1_out;

  not not_1 (not_1_out, I_3_0[0]);
  not not_2 (not_2_out, I_3_0[1]);
  not not_3 (not_3_out, I_3_0[2]);
  not not_4 (not_4_out, I_3_0[1]);
  not not_5 (not_5_out, I_3_0[2]);
  not not_6 (not_6_out, I_3_0[0]);
  not not_7 (not_7_out, I_3_0[2]);
  not not_8 (not_8_out, I_3_0[2]);
  not not_9 (not_9_out, I_3_0[0]);
  not not_10 (not_10_out, I_3_0[1]);
  not not_11 (not_11_out, I_3_0[1]);
  not not_12 (not_12_out, I_3_0[0]);
  and and_1 (and_1_out, not_1_out, not_2_out, not_3_out, I_3_0[3]);
  and and_2 (and_2_out, I_3_0[0], not_4_out, not_5_out, I_3_0[3]);
  and and_3 (and_3_out, not_6_out, I_3_0[1], not_7_out, I_3_0[3]);
  and and_4 (and_4_out, I_3_0[0], I_3_0[1], not_8_out, I_3_0[3]);
  and and_5 (and_5_out, not_9_out, not_10_out, I_3_0[2], I_3_0[3]);
  and and_6 (and_6_out, I_3_0[0], not_11_out, I_3_0[2], I_3_0[3]);
  and and_7 (and_7_out, not_12_out, I_3_0[1], I_3_0[2], I_3_0[3]);
  Multiplexer #(.Bits(4)) multiplexer_1 (.sel(JG8), .in_0(I_3_0), .in_1(4'b1111), .out(multiplexer_1_out));
  Add #(.Bits(4)) ADD1 (.a(multiplexer_1_out), .b(4'b0001), .c_i(1'b0), .s(O_3_0));  // open: c_o
  or or_1 (JG8, and_1_out, and_2_out, and_3_out, and_4_out, and_5_out, and_6_out, and_7_out);

  // Other names for the same wires on the sheet: I0 = I_3_0[0]; I1 = I_3_0[1]; I2 = I_3_0[2]; I3 = I_3_0[3]
endmodule
