// Digital circuit 5 Bit CPU.dig as structural Verilog
module _5_Bit_CPU (
  input  [3:0] WA_3_0,
  input  [14:0] WD_14_0,
  input  WE,
  input  CLK,
  input  PC_EN,
  input  [3:0] RA2,
  output [14:0] RD2,
  output [4:0] RS_4_0
);

  wire _5bitalu_1_cf, _5bitalu_1_sf, _5bitalu_1_zf, CF, CPU_CLK, Imm_SEL, JMP_SEL, R1, R2, Reg_EN, SF, ZF;
  wire [1:0] OP;
  wire [3:0] _4_bit_register_1_o_3_0, _4bit_pc_adder_1_o_3_0, JMP_ADD, multiplexer_1_out, OPCode;
  wire [4:0] _5_bit_reg_set_with_3_reg_1_p4, _5_bit_reg_set_with_3_reg_1_p6, Const, multiplexer_2_out;
  wire [10:0] Operand;

  Multiplexer #(.Bits(4)) multiplexer_1 (
    .sel(JMP_SEL), .in_0(_4bit_pc_adder_1_o_3_0), .in_1(JMP_ADD), .out(multiplexer_1_out));
  _4Bit_PC_Adder _4bit_pc_adder_1 (.I_3_0(_4_bit_register_1_o_3_0), .O_3_0(_4bit_pc_adder_1_o_3_0));
  _4_Bit_Register _4_bit_register_1 (.I_3_0(multiplexer_1_out), .CLK(CPU_CLK), .O_3_0(_4_bit_register_1_o_3_0));
  and and_1 (CPU_CLK, PC_EN, CLK);
  _9x15_RAM _9x15_ram_1 (
    .RA1_3_0(_4_bit_register_1_o_3_0), .RA2_3_0(RA2), .WA_3_0(WA_3_0), .WD_14_0(WD_14_0), .WE(WE), .CLK(CLK),
    .RD1_14_0({OPCode, Operand}), .RD2_14_0(RD2));
  // OPR opr_1: pin names not known; wires that end beside it: Operand, JMP_ADD, Const, R2, R1
  CUnit cunit_1 (.OPCode(OPCode), .ZF(ZF), .OP(OP), .Reg_EN(Reg_EN), .Imm_SEL(Imm_SEL), .Jmp_SEL(JMP_SEL));
  // _5_Bit_Reg_Set_with_3_Reg _5_bit_reg_set_with_3_reg_1: pin names not known; wires that end beside it: R1, CPU_CLK, R1, _5_bit_reg_set_with_3_reg_1_p4, R2, _5_bit_reg_set_with_3_reg_1_p6, Reg_EN, RS_4_0
  _5BitALU _5bitalu_1 (
    .A_4_0(_5_bit_reg_set_with_3_reg_1_p4), .B_4_0(multiplexer_2_out), .OP_1_0(OP), .R_4_0(RS_4_0),
    .CF(_5bitalu_1_cf), .SF(_5bitalu_1_sf), .ZF(_5bitalu_1_zf));
  Flag_Reg flag_reg_1 (
    .CLK(CPU_CLK), .CF_In(_5bitalu_1_cf), .SF_In(_5bitalu_1_sf), .ZF_In(_5bitalu_1_zf), .CF_Out(CF),
    .SF_Out(SF), .ZF_Out(ZF));
  Multiplexer #(.Bits(5)) multiplexer_2 (
    .sel(Imm_SEL), .in_0(_5_bit_reg_set_with_3_reg_1_p6), .in_1(Const), .out(multiplexer_2_out));

  // Notes on the sheet:
  //   CLK: Hz: 2
endmodule
