// Digital circuit 5 Bit Reg_Set with 3 Reg.dig as structural Verilog
module _5_Bit_Reg_Set_with_3_Reg (
  input  [1:0] WR_1_0,
  input  Reg_EN,
  input  [4:0] WRD_4_0,
  input  CLK,
  input  [1:0] Ra_1_0,
  input  [1:0] Rb_1_0,
  output [4:0] A_4_0,
  output [4:0] B_4_0
);

  wire D0, D1, D2, WR0, WR1, WR2;
  wire [4:0] R0, R1, R2;

  and and_1 (D2, WR2, Reg_EN);
  and and_2 (D1, WR1, Reg_EN);
  and and_3 (D0, WR0, Reg_EN);
  Decoder #(.Selector_Bits(2)) decoder_1 (.sel(WR_1_0), .out_0(WR0), .out_1(WR1), .out_2(WR2));  // open: out_3
  _5Bit_Register _5bit_register_1 (.Din_4_0(WRD_4_0), .SEL(D2), .CLK(CLK), .Dout_4_0(R2));
  _5Bit_Register _5bit_register_2 (.Din_4_0(WRD_4_0), .SEL(D1), .CLK(CLK), .Dout_4_0(R1));
  _5Bit_Register _5bit_register_3 (.Din_4_0(WRD_4_0), .SEL(D0), .CLK(CLK), .Dout_4_0(R0));
  Multiplexer #(.Selector_Bits(2), .Bits(5)) multiplexer_1 (
    .sel(Ra_1_0), .in_0(R0), .in_1(R1), .in_2(R2), .in_3({5{1'b0}}), .out(A_4_0));
  Multiplexer #(.Selector_Bits(2), .Bits(5)) multiplexer_2 (
    .sel(Rb_1_0), .in_0(R0), .in_1(R1), .in_2(R2), .in_3({5{1'b0}}), .out(B_4_0));

  // Other names for the same wires on the sheet: A[4:0] = A_4_0; B[4:0] = B_4_0; Ra[1:0] = Ra_1_0; Rb[1:0] = Rb_1_0;
  //   WRD[4:0] = WRD_4_0

  // Notes on the sheet:
  //   2x4 Decd
  //   4x1 MUX
endmodule
