// Digital circuit 5Bit Register.dig as structural Verilog
module _5Bit_Register (
  input  [4:0] Din_4_0,
  input  SEL,
  input  CLK,
  output [4:0] Dout_4_0
);

  _1_Bit_Reg _1_bit_reg_1 (.Din(Din_4_0[4]), .SEL(SEL), .CLK(CLK), .Dout(Dout_4_0[4]));
  _1_Bit_Reg _1_bit_reg_2 (.Din(Din_4_0[3]), .SEL(SEL), .CLK(CLK), .Dout(Dout_4_0[3]));
  _1_Bit_Reg _1_bit_reg_3 (.Din(Din_4_0[2]), .SEL(SEL), .CLK(CLK), .Dout(Dout_4_0[2]));
  _1_Bit_Reg _1_bit_reg_4 (.Din(Din_4_0[1]), .SEL(SEL), .CLK(CLK), .Dout(Dout_4_0[1]));
  _1_Bit_Reg _1_bit_reg_5 (.Din(Din_4_0[0]), .SEL(SEL), .CLK(CLK), .Dout(Dout_4_0[0]));

  // Other names for the same wires on the sheet: D0 = Dout_4_0[0]; D1 = Dout_4_0[1]; D2 = Dout_4_0[2];
  //   D3 = Dout_4_0[3]; D4 = Dout_4_0[4]; A0 = Din_4_0[0]; A1 = Din_4_0[1]; A2 = Din_4_0[2]; A3 = Din_4_0[3];
  //   A4 = Din_4_0[4]
endmodule
