// Digital circuit 5BitALU.dig as structural Verilog
module _5BitALU (
  input  [4:0] A_4_0,
  input  [4:0] B_4_0,
  input  [1:0] OP_1_0,
  output [4:0] R_4_0,
  output CF,
  output ZF,
  output SF
);

  wire [4:0] _5bitadder_1_s_4_0, _5bitshl_1_shl_4_0, _5bitxor_1_r_4_0;

  _5BitXOR _5bitxor_1 (.X_4_0(A_4_0), .Y_4_0(B_4_0), .R_4_0(_5bitxor_1_r_4_0));
  _5BitAdder _5bitadder_1 (.X_4_0(A_4_0), .Y_4_0(B_4_0), .S_4_0(_5bitadder_1_s_4_0), .Cout(CF));
  _5BitSHL _5bitshl_1 (.X_4_0(A_4_0), .Y_4_0(B_4_0), .SHL_4_0(_5bitshl_1_shl_4_0));
  Multiplexer #(.Selector_Bits(2), .Bits(5)) multiplexer_1 (
    .sel(OP_1_0), .in_0(_5bitxor_1_r_4_0), .in_1(_5bitadder_1_s_4_0), .in_2(_5bitshl_1_shl_4_0),
    .in_3({5{1'b0}}), .out(R_4_0));
  nor nor_1 (ZF, R_4_0[0], R_4_0[1], R_4_0[2], R_4_0[3], R_4_0[4]);

  assign SF = R_4_0[4];

  // Other names for the same wires on the sheet: A[4:0] = A_4_0; B[4:0] = B_4_0; OP[1:0] = OP_1_0
endmodule
