// Digital circuit 5BitAdder.dig as structural Verilog
module _5BitAdder (
  input  [4:0] X_4_0,
  input  [4:0] Y_4_0,
  output [4:0] S_4_0,
  output Cout
);

  wire f_add_2_c, f_add_3_c, f_add_4_c, f_add_5_c;

  F_Add f_add_1 (.Y(Y_4_0[4]), .X(X_4_0[4]), .Z(f_add_2_c), .S(S_4_0[4]), .C(Cout));
  F_Add f_add_2 (.Y(Y_4_0[3]), .X(X_4_0[3]), .Z(f_add_3_c), .S(S_4_0[3]), .C(f_add_2_c));
  F_Add f_add_3 (.Y(Y_4_0[2]), .X(X_4_0[2]), .Z(f_add_4_c), .S(S_4_0[2]), .C(f_add_3_c));
  F_Add f_add_4 (.Y(Y_4_0[1]), .X(X_4_0[1]), .Z(f_add_5_c), .S(S_4_0[1]), .C(f_add_4_c));
  F_Add f_add_5 (.Y(Y_4_0[0]), .X(X_4_0[0]), .Z(1'b0), .S(S_4_0[0]), .C(f_add_5_c));

  // Other names for the same wires on the sheet: Co = Cout
endmodule
