// Digital circuit 5BitSHL.dig as structural Verilog
module _5BitSHL (
  input  [4:0] X_4_0,
  input  [4:0] Y_4_0,
  output [4:0] SHL_4_0
);

  Multiplexer #(.Selector_Bits(3)) multiplexer_1 (
    .sel(Y_4_0[2:0]), .in_0(X_4_0[4]), .in_1(X_4_0[3]), .in_2(X_4_0[2]), .in_3(X_4_0[1]), .in_4(X_4_0[0]),
    .in_5(1'b0), .in_6(1'b0), .in_7(1'b0), .out(SHL_4_0[4]));
  Multiplexer #(.Selector_Bits(3)) multiplexer_2 (
    .sel(Y_4_0[2:0]), .in_0(X_4_0[3]), .in_1(X_4_0[2]), .in_2(X_4_0[1]), .in_3(X_4_0[0]), .in_4(1'b0),
    .in_5(1'b0), .in_6(1'b0), .in_7(1'b0), .out(SHL_4_0[3]));
  Multiplexer #(.Selector_Bits(3)) multiplexer_3 (
    .sel(Y_4_0[2:0]), .in_0(X_4_0[2]), .in_1(X_4_0[1]), .in_2(X_4_0[0]), .in_3(1'b0), .in_4(1'b0),
    .in_5(1'b0), .in_6(1'b0), .in_7(1'b0), .out(SHL_4_0[2]));
  Multiplexer #(.Selector_Bits(3)) multiplexer_4 (
    .sel(Y_4_0[2:0]), .in_0(X_4_0[1]), .in_1(X_4_0[0]), .in_2(1'b0), .in_3(1'b0), .in_4(1'b0), .in_5(1'b0),
    .in_6(1'b0), .in_7(1'b0), .out(SHL_4_0[1]));
  Multiplexer #(.Selector_Bits(3)) multiplexer_5 (
    .sel(Y_4_0[2:0]), .in_0(X_4_0[0]), .in_1(1'b0), .in_2(1'b0), .in_3(1'b0), .in_4(1'b0), .in_5(1'b0),
    .in_6(1'b0), .in_7(1'b0), .out(SHL_4_0[0]));

  // Other names for the same wires on the sheet: x0 = X_4_0[0]; x1 = X_4_0[1]; x2 = X_4_0[2]; x3 = X_4_0[3];
  //   x4 = X_4_0[4]; y_2_0[2:0] = Y_4_0[2:0]

  // Notes on the sheet:
  //   8x1 MUX
endmodule
