// Digital circuit 9x15 RAM.dig as structural Verilog
module _9x15_RAM (
  input  [3:0] RA1_3_0,
  input  [3:0] RA2_3_0,
  input  [3:0] WA_3_0,
  input  [14:0] WD_14_0,
  input  CLK,
  input  WE,
  output [14:0] RD2_14_0,
  output [14:0] RD1_14_0
);

  wire and_1_out, and_2_out, and_3_out, and_4_out, and_5_out, and_6_out, and_7_out, and_8_out, and_9_out,
       RA1_0, RA1_1, RA1_2, RA1_3, RA1_4, RA1_5, RA1_6, RA1_7, RA1_8, RA2_0, RA2_1, RA2_2, RA2_3, RA2_4,
       RA2_5, RA2_6, RA2_7, RA2_8, WA_0, WA_1, WA_2, WA_3, WA_4, WA_5, WA_6, WA_7, WA_8;
  wire [14:0] RD1_0, RD1_1, RD1_2, RD1_3, RD1_4, RD1_5, RD1_6, RD1_7, RD1_8, RD2_0, RD2_1, RD2_2, RD2_3,
       RD2_4, RD2_5, RD2_6, RD2_7, RD2_8;

  Decoder #(.Selector_Bits(4)) decoder_1 (
    .sel(RA2_3_0), .out_0(RA2_0), .out_1(RA2_1), .out_2(RA2_2), .out_3(RA2_3), .out_4(RA2_4), .out_5(RA2_5),
    .out_6(RA2_6), .out_7(RA2_7), .out_8(RA2_8));  // open: out_9, out_10, out_11, out_12, out_13, out_14, out_15
  Decoder #(.Selector_Bits(4)) decoder_2 (
    .sel(WA_3_0), .out_0(WA_0), .out_1(WA_1), .out_2(WA_2), .out_3(WA_3), .out_4(WA_4), .out_5(WA_5),
    .out_6(WA_6), .out_7(WA_7), .out_8(WA_8));  // open: out_9, out_10, out_11, out_12, out_13, out_14, out_15
  Decoder #(.Selector_Bits(4)) decoder_3 (
    .sel(RA1_3_0), .out_0(RA1_0), .out_1(RA1_1), .out_2(RA1_2), .out_3(RA1_3), .out_4(RA1_4), .out_5(RA1_5),
    .out_6(RA1_6), .out_7(RA1_7), .out_8(RA1_8));  // open: out_9, out_10, out_11, out_12, out_13, out_14, out_15
  and and_1 (and_1_out, WA_8, WE);
  and and_2 (and_2_out, WA_7, WE);
  and and_3 (and_3_out, WA_6, WE);
  and and_4 (and_4_out, WA_5, WE);
  and and_5 (and_5_out, WA_4, WE);
  and and_6 (and_6_out, WA_3, WE);
  and and_7 (and_7_out, WA_2, WE);
  and and_8 (and_8_out, WA_1, WE);
  and and_9 (and_9_out, WA_0, WE);
  _1x15_RAM _1x15_ram_1 (
    .RS1(RA1_8), .RS2(RA2_8), .WS(and_1_out), .WD_14_0(WD_14_0), .CLK(CLK), .RD1_14_0(RD1_8), .RD2_14_0(RD2_8));
  _1x15_RAM _1x15_ram_2 (
    .RS1(RA1_7), .RS2(RA2_7), .WS(and_2_out), .WD_14_0(WD_14_0), .CLK(CLK), .RD1_14_0(RD1_7), .RD2_14_0(RD2_7));
  _1x15_RAM _1x15_ram_3 (
    .RS1(RA1_6), .RS2(RA2_6), .WS(and_3_out), .WD_14_0(WD_14_0), .CLK(CLK), .RD1_14_0(RD1_6), .RD2_14_0(RD2_6));
  _1x15_RAM _1x15_ram_4 (
    .RS1(RA1_5), .RS2(RA2_5), .WS(and_4_out), .WD_14_0(WD_14_0), .CLK(CLK), .RD1_14_0(RD1_5), .RD2_14_0(RD2_5));
  _1x15_RAM _1x15_ram_5 (
    .RS1(RA1_4), .RS2(RA2_4), .WS(and_5_out), .WD_14_0(WD_14_0), .CLK(CLK), .RD1_14_0(RD1_4), .RD2_14_0(RD2_4));
  _1x15_RAM _1x15_ram_6 (
    .RS1(RA1_3), .RS2(RA2_3), .WS(and_6_out), .WD_14_0(WD_14_0), .CLK(CLK), .RD1_14_0(RD1_3), .RD2_14_0(RD2_3));
  _1x15_RAM _1x15_ram_7 (
    .RS1(RA1_2), .RS2(RA2_2), .WS(and_7_out), .WD_14_0(WD_14_0), .CLK(CLK), .RD1_14_0(RD1_2), .RD2_14_0(RD2_2));
  _1x15_RAM _1x15_ram_8 (
    .RS1(RA1_1), .RS2(RA2_1), .WS(and_8_out), .WD_14_0(WD_14_0), .CLK(CLK), .RD1_14_0(RD1_1), .RD2_14_0(RD2_1));
  _1x15_RAM _1x15_ram_9 (
    .RS1(RA1_0), .RS2(RA2_0), .WS(and_9_out), .WD_14_0(WD_14_0), .CLK(CLK), .RD1_14_0(RD1_0), .RD2_14_0(RD2_0));
  assign RD1_14_0 = RD1_0 | RD1_1 | RD1_2 | RD1_3 | RD1_4 | RD1_5 | RD1_6 | RD1_7 | RD1_8;  // Or or_1, 15 bits wide
  assign RD2_14_0 = RD2_0 | RD2_1 | RD2_2 | RD2_3 | RD2_4 | RD2_5 | RD2_6 | RD2_7 | RD2_8;  // Or or_2, 15 bits wide

  // Other names for the same wires on the sheet: WD[14:0] = WD_14_0

  // Notes on the sheet:
  //   4x16 Decd
endmodule
