// Digital circuit CUnit.dig as structural Verilog
module CUnit (
  input  [3:0] OPCode,
  input  ZF,
  output [1:0] OP,
  output Reg_EN,
  output Imm_SEL,
  output Jmp_SEL
);

  wire and_1_out, and_2_out, and_3_out, and_4_out, not_1_out, not_2_out, not_3_out, not_4_out, not_5_out,
       not_6_out, not_7_out, not_8_out, or_1_out;

  not not_1 (not_1_out, ZF);
  not not_2 (not_2_out, OPCode[2]);
  not not_3 (not_3_out, OPCode[0]);
  not not_4 (not_4_out, OPCode[1]);
  not not_5 (not_5_out, OPCode[1]);
  and and_1 (and_1_out, not_2_out, OPCode[3]);
  and and_2 (and_2_out, not_3_out, not_4_out);
  and and_3 (and_3_out, OPCode[0], not_1_out, not_5_out);
  not not_6 (not_6_out, OPCode[2]);
  not not_7 (not_7_out, OPCode[3]);
  not not_8 (not_8_out, OPCode[3]);
  or or_1 (or_1_out, and_2_out, and_3_out);
  and and_4 (and_4_out, not_6_out, not_7_out);
  and and_5 (Imm_SEL, OPCode[2], not_8_out);
  and and_6 (Jmp_SEL, and_1_out, or_1_out);
  or or_2 (Reg_EN, and_4_out, Imm_SEL);

  assign OP = OPCode[1:0];

  // Other names for the same wires on the sheet: OPC1 = OPCode[0]; OPC2 = OPCode[1]; OPC3 = OPCode[2];
  //   OPC4 = OPCode[3]
endmodule
