// Digital circuit Flag Reg.dig as structural Verilog
module Flag_Reg (
  input  CLK,
  input  CF_In,
  input  SF_In,
  input  ZF_In,
  output CF_Out,
  output SF_Out,
  output ZF_Out
);

  _1_Bit_Reg _1_bit_reg_1 (.Din(CF_In), .SEL(1'b1), .CLK(CLK), .Dout(CF_Out));
  _1_Bit_Reg _1_bit_reg_2 (.Din(SF_In), .SEL(1'b1), .CLK(CLK), .Dout(SF_Out));
  _1_Bit_Reg _1_bit_reg_3 (.Din(ZF_In), .SEL(1'b1), .CLK(CLK), .Dout(ZF_Out));

  // Other names for the same wires on the sheet: A1 = CF_In; A2 = SF_In; A3 = ZF_In; B1 = CF_Out; B2 = SF_Out;
  //   B3 = ZF_Out
endmodule
