// Digital circuit OPR.dig as structural Verilog
module OPR (
  input  [10:0] OpR,
  output [1:0] R2,
  output [1:0] R1,
  output [4:0] Const,
  output [3:0] JAD_3_0
);

  // Pins of 1 and 2 bits meet at OpR[8:7]
  // Pins of 1 and 2 bits meet at OpR[10:9]
  // Pins of 1 and 5 bits meet at OpR[8:4]
  // Pins of 3 and 4 bits meet at OpR[10:7]

  assign Const = OpR[8:4];
  assign JAD_3_0 = OpR[10:7];
  assign R1 = OpR[10:9];
  assign R2 = OpR[8:7];
endmodule
